// Logisim project processor.circ as structural Verilog: 13 circuits, main circuit Processor
module _16_bit_register (
  input  Write,
  input  Clock,
  input  [15:0] D___In,
  output [15:0] D___Out
);

  D_Flip_Flop d_ff_1 (.clk(Clock), .D(D___In[0]), .Q(D___Out[0]), .en(Write));  // open: Qn, preset, reset
  D_Flip_Flop d_ff_2 (.clk(Clock), .D(D___In[1]), .Q(D___Out[1]), .en(Write));  // open: Qn, preset, reset
  D_Flip_Flop d_ff_3 (.clk(Clock), .D(D___In[2]), .Q(D___Out[2]), .en(Write));  // open: Qn, preset, reset
  D_Flip_Flop d_ff_4 (.clk(Clock), .D(D___In[3]), .Q(D___Out[3]), .en(Write));  // open: Qn, preset, reset
  D_Flip_Flop d_ff_5 (.clk(Clock), .D(D___In[4]), .Q(D___Out[4]), .en(Write));  // open: Qn, preset, reset
  D_Flip_Flop d_ff_6 (.clk(Clock), .D(D___In[5]), .Q(D___Out[5]), .en(Write));  // open: Qn, preset, reset
  D_Flip_Flop d_ff_7 (.clk(Clock), .D(D___In[6]), .Q(D___Out[6]), .en(Write));  // open: Qn, preset, reset
  D_Flip_Flop d_ff_8 (.clk(Clock), .D(D___In[7]), .Q(D___Out[7]), .en(Write));  // open: Qn, preset, reset
  D_Flip_Flop d_ff_9 (.clk(Clock), .D(D___In[8]), .Q(D___Out[8]), .en(Write));  // open: Qn, preset, reset
  D_Flip_Flop d_ff_10 (.clk(Clock), .D(D___In[9]), .Q(D___Out[9]), .en(Write));  // open: Qn, preset, reset
  D_Flip_Flop d_ff_11 (.clk(Clock), .D(D___In[10]), .Q(D___Out[10]), .en(Write));  // open: Qn, preset, reset
  D_Flip_Flop d_ff_12 (.clk(Clock), .D(D___In[11]), .Q(D___Out[11]), .en(Write));  // open: Qn, preset, reset
  D_Flip_Flop d_ff_13 (.clk(Clock), .D(D___In[12]), .Q(D___Out[12]), .en(Write));  // open: Qn, preset, reset
  D_Flip_Flop d_ff_14 (.clk(Clock), .D(D___In[13]), .Q(D___Out[13]), .en(Write));  // open: Qn, preset, reset
  D_Flip_Flop d_ff_15 (.clk(Clock), .D(D___In[14]), .Q(D___Out[14]), .en(Write));  // open: Qn, preset, reset
  D_Flip_Flop d_ff_16 (.clk(Clock), .D(D___In[15]), .Q(D___Out[15]), .en(Write));  // open: Qn, preset, reset
endmodule

module Register_Set (
  input  RegWrite,
  input  Clock,
  input  [2:0] RW,
  input  [2:0] RA,
  input  [15:0] Bus_W,
  input  [2:0] RB,
  output [15:0] Bus_A,
  output [15:0] Bus_B
);

  wire decoder_1_out1, decoder_1_out2, decoder_1_out3, decoder_1_out4, decoder_1_out5, decoder_1_out6,
       decoder_1_out7;
  wire [15:0] R1_d___out, R2_d___out, R3_d___out, R4_d___out, R5_d___out, R6_d___out, R7_d___out;

  Decoder #(.select(3)) decoder_1 (
    .out1(decoder_1_out1), .out2(decoder_1_out2), .out3(decoder_1_out3), .out4(decoder_1_out4),
    .out5(decoder_1_out5), .out6(decoder_1_out6), .out7(decoder_1_out7), .sel(RW), .en(RegWrite));  // open: out0
  _16_bit_register R1 (.D___In(Bus_W), .D___Out(R1_d___out), .Write(decoder_1_out1), .Clock(Clock));
  _16_bit_register R2 (.D___In(Bus_W), .D___Out(R2_d___out), .Write(decoder_1_out2), .Clock(Clock));
  _16_bit_register R3 (.D___In(Bus_W), .D___Out(R3_d___out), .Write(decoder_1_out3), .Clock(Clock));
  _16_bit_register R4 (.D___In(Bus_W), .D___Out(R4_d___out), .Write(decoder_1_out4), .Clock(Clock));
  _16_bit_register R5 (.D___In(Bus_W), .D___Out(R5_d___out), .Write(decoder_1_out5), .Clock(Clock));
  _16_bit_register R6 (.D___In(Bus_W), .D___Out(R6_d___out), .Write(decoder_1_out6), .Clock(Clock));
  _16_bit_register R7 (.D___In(Bus_W), .D___Out(R7_d___out), .Write(decoder_1_out7), .Clock(Clock));
  Multiplexer #(.select(3), .width(16), .enable("false")) multiplexer_1 (
    .in0({16{1'b0}}), .in1(R1_d___out), .in2(R2_d___out), .in3(R3_d___out), .in4(R4_d___out),
    .in5(R5_d___out), .in6(R6_d___out), .in7(R7_d___out), .out(Bus_A), .sel(RA));
  Multiplexer #(.select(3), .width(16), .enable("false")) multiplexer_2 (
    .in0({16{1'b0}}), .in1(R1_d___out), .in2(R2_d___out), .in3(R3_d___out), .in4(R4_d___out),
    .in5(R5_d___out), .in6(R6_d___out), .in7(R7_d___out), .out(Bus_B), .sel(RB));

  // Notes on the sheet:
  //   R0
endmodule

module Extender (
  input  [4:0] Immediate,
  input  ExtOp,
  output [15:0] Out
);

  wire [15:0] bit_extender_1_out, bit_extender_2_out;

  assign bit_extender_1_out = {{11{1'b0}}, Immediate};  // Bit_Extender bit_extender_1
  Multiplexer #(.width(16)) multiplexer_1 (
    .in0(bit_extender_1_out), .in1(bit_extender_2_out), .out(Out), .sel(ExtOp));  // open: en
  assign bit_extender_2_out = {{11{Immediate[4]}}, Immediate};  // Bit_Extender bit_extender_2
endmodule

module ALU (
  input  [3:0] ALUCtrl,
  input  [15:0] Bus_A,
  input  [15:0] Bus_B,
  output JR,
  output [15:0] Output,
  output Zero
);

  wire comparator_1_lt, comparator_2_lt;
  wire [3:0] bitselector_1_out;
  wire [15:0] adder_1_out, AND_out, bit_extender_1_out, bit_extender_2_out, NOR_out, OR_out, shifter_1_out,
       shifter_2_out, shifter_3_out, shifter_4_out, subtractor_1_out, XOR_out;

  BitSelector #(.width(16), .group(4)) bitselector_1 (.in(Bus_B), .out(bitselector_1_out), .sel(2'b00));
  assign AND_out = Bus_A & Bus_B;  // AND_Gate AND, 16 bits wide
  assign OR_out = Bus_A | Bus_B;  // OR_Gate OR, 16 bits wide
  assign XOR_out = Bus_A ^ Bus_B;  // XOR_Gate XOR, 16 bits wide
  assign NOR_out = ~(Bus_A | Bus_B);  // NOR_Gate NOR, 16 bits wide
  Adder #(.width(16)) adder_1 (.a(Bus_A), .b(Bus_B), .out(adder_1_out));  // open: cin, cout
  Subtractor #(.width(16)) subtractor_1 (.a(Bus_A), .b(Bus_B), .out(subtractor_1_out));  // open: bin, bout
  Comparator #(.width(16)) comparator_1 (.a(Bus_A), .b(Bus_B), .lt(comparator_1_lt));  // open: gt, eq
  Comparator #(.width(16), .mode("unsigned")) comparator_2 (
    .a(Bus_A), .b(Bus_B), .lt(comparator_2_lt));  // open: gt, eq
  Shifter #(.width(16)) shifter_1 (.in(Bus_A), .\dist (bitselector_1_out), .out(shifter_1_out));
  Shifter #(.width(16), .shift("lr")) shifter_2 (.in(Bus_A), .\dist (bitselector_1_out), .out(shifter_2_out));
  Shifter #(.width(16), .shift("ar")) shifter_3 (.in(Bus_A), .\dist (bitselector_1_out), .out(shifter_3_out));
  Shifter #(.width(16), .shift("rr")) shifter_4 (.in(Bus_A), .\dist (bitselector_1_out), .out(shifter_4_out));
  assign bit_extender_1_out = {{15{1'b0}}, comparator_1_lt};  // Bit_Extender bit_extender_1
  assign bit_extender_2_out = {{15{1'b0}}, comparator_2_lt};  // Bit_Extender bit_extender_2
  Multiplexer #(.select(4), .width(16), .enable("false")) multiplexer_1 (
    .in0(AND_out), .in1(OR_out), .in2(XOR_out), .in3(NOR_out), .in4(adder_1_out), .in5(subtractor_1_out),
    .in6(bit_extender_1_out), .in7(Bus_A), .in8(shifter_1_out), .in9(shifter_2_out), .in10(shifter_3_out),
    .in11(shifter_4_out), .in12(bit_extender_2_out), .out(Output), .sel(ALUCtrl));  // open: in13, in14, in15
  and and_2 (JR, ALUCtrl[3], ALUCtrl[2], ALUCtrl[1], ~ALUCtrl[0]);  // AND_Gate
  nor nor_2 (Zero, Output[15], Output[14], Output[13], Output[12], Output[11], Output[10], Output[9], Output[8], Output[7], Output[6], Output[5], Output[4], Output[3], Output[2], Output[1], Output[0]);

  // Notes on the sheet:
  //   ADD
  //   SUB
  //   SLT
  //   SLTU
  //   SLL
  //   SRL
  //   SRA
  //   ROR
endmodule

module ALUCtrl (
  input  [4:0] Opcode,
  input  [1:0] Function,
  input  [3:0] Main_Control,
  input  Type,
  output [3:0] ALU_Control,
  output LWS
);

  wire ADD_out, AND_out, JR_out, NOR_out, OR_out, RType_2_out, RType_3_out, RType_out, SLT_out, SLTU_out,
       SUB_out, XOR_out;
  wire [3:0] priority_encoder_1_out;

  and RType (RType_out, ~Opcode[4], ~Opcode[3], ~Opcode[2], Opcode[1], ~Opcode[0]);  // AND_Gate
  and JR (JR_out, ~Function[1], ~Function[0], RType_out);  // AND_Gate
  and RType_2 (RType_2_out, ~Opcode[4], ~Opcode[3], ~Opcode[2], ~Opcode[1], Opcode[0]);  // AND_Gate
  and ADD (ADD_out, ~Function[1], ~Function[0], RType_2_out);  // AND_Gate
  and SUB (SUB_out, ~Function[1], Function[0], RType_2_out);  // AND_Gate
  and SLT (SLT_out, Function[1], ~Function[0], RType_2_out);  // AND_Gate
  and RType_3 (RType_3_out, ~Opcode[4], ~Opcode[3], ~Opcode[2], ~Opcode[1], ~Opcode[0]);  // AND_Gate
  and SLTU (SLTU_out, Function[1], Function[0], RType_2_out);
  and AND (AND_out, ~Function[1], ~Function[0], RType_3_out);  // AND_Gate
  and OR (OR_out, ~Function[1], Function[0], RType_3_out);  // AND_Gate
  and XOR (XOR_out, Function[1], ~Function[0], RType_3_out);  // AND_Gate
  and NOR (NOR_out, Function[1], Function[0], RType_3_out);
  Multiplexer #(.width(4), .enable("false")) multiplexer_1 (
    .in0(Main_Control), .in1(priority_encoder_1_out), .out(ALU_Control), .sel(Type));
  Priority_Encoder #(.select(4)) priority_encoder_1 (
    .in0(AND_out), .in1(OR_out), .in2(XOR_out), .in3(NOR_out), .in4(ADD_out), .in5(SUB_out), .in6(SLT_out),
    .in7(JR_out), .in12(SLTU_out), .out(priority_encoder_1_out));  // open: in8, in9, in10, in11, in13, in14, in15, gs, en_out, en_in
  and and_2 (LWS, ~ALU_Control[0], ~ALU_Control[1], ALU_Control[2], ~ALU_Control[3]);  // AND_Gate
endmodule

module Program_Counter_Control (
  input  BNE,
  input  Zero,
  input  BEQ,
  input  Jump,
  input  JR,
  input  [2:0] Rs,
  output [2:0] PC
);

  wire and_2_out, and_3_out;
  wire [2:1] and_4_out;

  and and_1 (and_4_out[2], BNE, ~Zero);  // AND_Gate
  and and_2 (and_2_out, ~and_3_out, JR);  // AND_Gate
  and and_3 (and_3_out, ~Rs[2], ~Rs[1], ~Rs[0]);  // AND_Gate
  and and_4 (and_4_out[1], Zero, BEQ);
  Multiplexer #(.width(3), .enable("false")) multiplexer_1 (
    .in0({and_4_out, Jump}), .in1(3'b111), .out(PC), .sel(and_2_out));
endmodule

module IF_Buffer (
  input  [15:0] PC_in,
  input  CLK,
  input  [15:0] IR_in,
  output [15:0] PC_out,
  output [15:0] IR_out
);

  Register #(.width(16)) register_1 (.D(PC_in), .Q(PC_out), .clk(CLK));  // open: en, clr
  Register #(.width(16)) register_2 (.D(IR_in), .Q(IR_out), .clk(CLK));  // open: en, clr
endmodule

module EX_buffer (
  input  [2:0] in_1,
  input  [15:0] ALU_In,
  input  [15:0] in_3,
  input  Clock,
  input  MW_In,
  input  MemRead_In,
  input  MemToReg_In,
  input  RW_In,
  output [2:0] out_9,
  output [15:0] ALU_Out,
  output [15:0] out_11,
  output MW_Out,
  output MemRead_Out,
  output MemToReg_Out,
  output RW_Out
);

  Register #(.width(3)) register_1 (.D(in_1), .Q(out_9), .clk(Clock));  // open: en, clr
  Register #(.width(16)) register_2 (.D(ALU_In), .Q(ALU_Out), .clk(Clock));  // open: en, clr
  Register #(.width(16)) register_3 (.D(in_3), .Q(out_11), .clk(Clock));  // open: en, clr
  Register #(.width(1)) register_4 (.D(MW_In), .Q(MW_Out), .clk(Clock));  // open: en, clr
  Register #(.width(1)) register_5 (.D(MemRead_In), .Q(MemRead_Out), .clk(Clock));  // open: en, clr
  Register #(.width(1)) register_6 (.D(MemToReg_In), .Q(MemToReg_Out), .clk(Clock));  // open: en, clr
  Register #(.width(1)) register_7 (.D(RW_In), .Q(RW_Out), .clk(Clock));  // open: en, clr
endmodule

module MEM_Buffer (
  input  [2:0] in_1,
  input  [15:0] ALU_In,
  input  [15:0] Mem_In,
  input  Clock,
  input  MTR_In,
  input  RW_In,
  output [2:0] out_7,
  output [15:0] ALU_Out,
  output [15:0] Mem_Out,
  output MTR_Out,
  output RE_Out
);

  Register #(.width(3)) register_1 (.D(in_1), .Q(out_7), .clk(Clock));  // open: en, clr
  Register #(.width(16)) register_2 (.D(ALU_In), .Q(ALU_Out), .clk(Clock));  // open: en, clr
  Register #(.width(16)) register_3 (.D(Mem_In), .Q(Mem_Out), .clk(Clock));  // open: en, clr
  Register #(.width(1)) register_4 (.D(MTR_In), .Q(MTR_Out), .clk(Clock));  // open: en, clr
  Register #(.width(1)) register_5 (.D(RW_In), .Q(RE_Out), .clk(Clock));  // open: en, clr
endmodule

module ID_Buffer (
  input  [15:0] JImm_In,
  input  [2:0] RA,
  input  [2:0] RB,
  input  [2:0] RD,
  input  [15:0] PC_In,
  input  [4:0] Imm_In,
  input  [15:0] Bus_A_In,
  input  [15:0] Bus_B_In,
  input  [3:0] ALUOp,
  input  JAL_In,
  input  Clock,
  input  Jump_In,
  input  RegDest_In,
  input  BEQ_In,
  input  MemWrite_In,
  input  MemRead_In,
  input  MemToReg_In,
  input  RegWrite_In,
  input  BNEQ_In,
  input  ALUSrc_In,
  input  ExtOp_In,
  output [15:0] JImm_Out,
  output [2:0] RA_Out,
  output [2:0] RB_Out,
  output [2:0] RD_Out,
  output [15:0] PC_Out,
  output [4:0] Imm_Out,
  output [15:0] Bus_A_Out,
  output [15:0] Bus_B_In_2,
  output [3:0] ALUOp_2,
  output JAL_Out,
  output Jump_Out,
  output RegDest_Out,
  output BEQ_Out,
  output MemWrite_Out,
  output MemRead_Out,
  output MemToReg_Out,
  output RegWrite_Out,
  output BNEQ_Out,
  output ALUSrc_Out,
  output ExtOp_Out
);

  Register #(.width(16)) register_1 (.D(JImm_In), .Q(JImm_Out), .clk(Clock));  // open: en, clr
  Register #(.width(3)) register_2 (.D(RA), .Q(RA_Out), .clk(Clock));  // open: en, clr
  Register #(.width(3)) register_3 (.D(RB), .Q(RB_Out), .clk(Clock));  // open: en, clr
  Register #(.width(3)) register_4 (.D(RD), .Q(RD_Out), .clk(Clock));  // open: en, clr
  Register #(.width(16)) register_5 (.D(PC_In), .Q(PC_Out), .clk(Clock));  // open: en, clr
  Register #(.width(5)) register_6 (.D(Imm_In), .Q(Imm_Out), .clk(Clock));  // open: en, clr
  Register #(.width(16)) register_7 (.D(Bus_A_In), .Q(Bus_A_Out), .clk(Clock));  // open: en, clr
  Register #(.width(16)) register_8 (.D(Bus_B_In), .Q(Bus_B_In_2), .clk(Clock));  // open: en, clr
  Register #(.width(4)) register_9 (.D(ALUOp), .Q(ALUOp_2), .clk(Clock));  // open: en, clr
  Register #(.width(1)) register_10 (.D(JAL_In), .Q(JAL_Out), .clk(Clock));  // open: en, clr
  Register #(.width(1)) register_11 (.D(Jump_In), .Q(Jump_Out), .clk(Clock));  // open: en, clr
  Register #(.width(1)) register_12 (.D(RegDest_In), .Q(RegDest_Out), .clk(Clock));  // open: en, clr
  Register #(.width(1)) register_13 (.D(BEQ_In), .Q(BEQ_Out), .clk(Clock));  // open: en, clr
  Register #(.width(1)) register_14 (.D(MemWrite_In), .Q(MemWrite_Out), .clk(Clock));  // open: en, clr
  Register #(.width(1)) register_15 (.D(MemRead_In), .Q(MemRead_Out), .clk(Clock));  // open: en, clr
  Register #(.width(1)) register_16 (.D(MemToReg_In), .Q(MemToReg_Out), .clk(Clock));  // open: en, clr
  Register #(.width(1)) register_17 (.D(RegWrite_In), .Q(RegWrite_Out), .clk(Clock));  // open: en, clr
  Register #(.width(1)) register_18 (.D(BNEQ_In), .Q(BNEQ_Out), .clk(Clock));  // open: en, clr
  Register #(.width(1)) register_19 (.D(ALUSrc_In), .Q(ALUSrc_Out), .clk(Clock));  // open: en, clr
  Register #(.width(1)) register_20 (.D(ExtOp_In), .Q(ExtOp_Out), .clk(Clock));  // open: en, clr
endmodule

module Forward (
  input  [2:0] RS,
  input  RegWrite_MEM,
  input  RegWrite_WB,
  input  [2:0] RD_MEM,
  input  [2:0] RD_WB,
  input  [2:0] RT,
  output [1:0] ForwardA,
  output [1:0] ForwardB
);

  wire comparator_1_eq, comparator_2_eq, comparator_3_eq, comparator_4_eq, comparator_5_eq, comparator_6_eq,
       comparator_7_eq, comparator_8_eq, comparator_9_eq, not_1_out, not_2_out, not_3_out, not_4_out,
       not_5_out;
  wire [0:0] and_3_out, and_4_out;
  wire [1:1] and_1_out, and_2_out;

  assign ForwardA = {and_1_out[1], 1'b0} | {1'b0, and_3_out[0]};  // OR_Gate or_1, 2 bits wide
  assign ForwardB = {and_2_out[1], 1'b0} | {1'b0, and_4_out[0]};  // OR_Gate or_2, 2 bits wide
  and and_1 (and_1_out[1], RegWrite_MEM, not_1_out, comparator_2_eq);
  and and_2 (and_2_out[1], RegWrite_MEM, not_2_out, comparator_4_eq);
  and and_3 (and_3_out[0], RegWrite_WB, not_3_out, not_4_out, comparator_7_eq);
  and and_4 (and_4_out[0], RegWrite_WB, comparator_5_eq, not_5_out, comparator_9_eq);
  not not_1 (not_1_out, comparator_1_eq);
  Comparator #(.width(3)) comparator_1 (.a(3'b000), .b(RD_MEM), .eq(comparator_1_eq));  // open: gt, lt
  Comparator #(.width(3)) comparator_2 (.a(RS), .b(RD_MEM), .eq(comparator_2_eq));  // open: gt, lt
  not not_2 (not_2_out, comparator_3_eq);
  Comparator #(.width(3)) comparator_3 (.a(3'b000), .b(RD_MEM), .eq(comparator_3_eq));  // open: gt, lt
  Comparator #(.width(3)) comparator_4 (.a(RT), .b(RD_MEM), .eq(comparator_4_eq));  // open: gt, lt
  not not_3 (not_3_out, comparator_5_eq);
  not not_4 (not_4_out, comparator_6_eq);
  Comparator #(.width(3)) comparator_5 (.a(3'b000), .b(RD_WB), .eq(comparator_5_eq));  // open: gt, lt
  Comparator #(.width(3)) comparator_6 (.a(RD_MEM), .b(RS), .eq(comparator_6_eq));  // open: gt, lt
  Comparator #(.width(3)) comparator_7 (.a(RD_WB), .b(RS), .eq(comparator_7_eq));  // open: gt, lt
  not not_5 (not_5_out, comparator_8_eq);
  Comparator #(.width(3)) comparator_8 (.a(RD_MEM), .b(RT), .eq(comparator_8_eq));  // open: gt, lt
  Comparator #(.width(3)) comparator_9 (.a(RD_WB), .b(RT), .eq(comparator_9_eq));  // open: gt, lt
endmodule

module Control_Unit (
  input  [4:0] Opcode,
  output JAL,
  output Jump,
  output RegDest,
  output BEQ,
  output MemWrite,
  output MemRead,
  output MemToReg,
  output LUI,
  output RegWrite,
  output BNEQ,
  output ALUSrc,
  output R_Type,
  output ExtOp,
  output [3:0] ALUOp
);

  wire ADDI_out, ANDI_out, BEQ_out, J_out, or_2_out, or_3_out, ORI_out, R_type_2_out, R_type_3_out,
       R_type_out, ROR_out, SLL_out, SRA_out, SRL_out, XORI_out;

  and u_R_type (R_type_out, ~Opcode[4], ~Opcode[3], ~Opcode[2], Opcode[1], ~Opcode[0]);  // AND_Gate
  and R_type_2 (R_type_2_out, ~Opcode[4], ~Opcode[3], ~Opcode[2], ~Opcode[1], Opcode[0]);  // AND_Gate
  or or_1 (R_Type, R_type_out, R_type_2_out, R_type_3_out);
  and R_type_3 (R_type_3_out, ~Opcode[4], ~Opcode[3], ~Opcode[2], ~Opcode[1], ~Opcode[0]);  // AND_Gate
  and LW (MemRead, ~Opcode[4], Opcode[3], Opcode[2], ~Opcode[1], ~Opcode[0]);  // AND_Gate
  and SW (MemWrite, ~Opcode[4], Opcode[3], Opcode[2], ~Opcode[1], Opcode[0]);  // AND_Gate
  or or_2 (or_2_out, MemRead, MemWrite, ADDI_out);
  and u_BEQ (BEQ_out, ~Opcode[4], Opcode[3], Opcode[2], Opcode[1], ~Opcode[0]);  // AND_Gate
  and ADDI (ADDI_out, ~Opcode[4], ~Opcode[3], Opcode[2], Opcode[1], Opcode[0]);  // AND_Gate
  or or_3 (or_3_out, BEQ_out, BNEQ);
  and SLL (SLL_out, ~Opcode[4], Opcode[3], ~Opcode[2], ~Opcode[1], ~Opcode[0]);  // AND_Gate
  and ANDI (ANDI_out, ~Opcode[4], ~Opcode[3], Opcode[2], ~Opcode[1], ~Opcode[0]);  // AND_Gate
  and ORI (ORI_out, ~Opcode[4], ~Opcode[3], Opcode[2], ~Opcode[1], Opcode[0]);  // AND_Gate
  and XORI (XORI_out, ~Opcode[4], ~Opcode[3], Opcode[2], Opcode[1], ~Opcode[0]);  // AND_Gate
  and SRL (SRL_out, ~Opcode[4], Opcode[3], ~Opcode[2], ~Opcode[1], Opcode[0]);  // AND_Gate
  and SRA (SRA_out, ~Opcode[4], Opcode[3], ~Opcode[2], Opcode[1], ~Opcode[0]);  // AND_Gate
  and ROR (ROR_out, ~Opcode[4], Opcode[3], ~Opcode[2], Opcode[1], Opcode[0]);  // AND_Gate
  and BNE (BNEQ, ~Opcode[4], Opcode[3], Opcode[2], Opcode[1], Opcode[0]);  // AND_Gate
  and J (J_out, Opcode[4], Opcode[3], Opcode[2], Opcode[1], ~Opcode[0]);  // AND_Gate
  and u_LUI (LUI, Opcode[4], ~Opcode[3], ~Opcode[2], ~Opcode[1], ~Opcode[0]);  // AND_Gate
  and u_JAL (JAL, Opcode[4], Opcode[3], Opcode[2], Opcode[1], Opcode[0]);
  Priority_Encoder #(.select(4)) priority_encoder_1 (
    .in0(ANDI_out), .in1(ORI_out), .in2(XORI_out), .in4(or_2_out), .in5(or_3_out), .in7(LUI), .in8(SLL_out),
    .in9(SRL_out), .in10(SRA_out), .in11(ROR_out), .out(ALUOp));  // open: in3, in6, in12, in13, in14, in15, gs, en_out, en_in
  or or_4 (RegWrite, JAL, MemRead, LUI, ANDI_out, ADDI_out, R_Type, ORI_out, XORI_out);
  or or_5 (ALUSrc, XORI_out, ORI_out, MemRead, R_Type, ORI_out, MemWrite, ADDI_out, ANDI_out);
  or or_6 (Jump, JAL, J_out);
  or or_7 (BEQ, BEQ_out, BNEQ);
  or or_8 (ExtOp, MemRead, MemWrite, ADDI_out, SLL_out, ANDI_out, ORI_out, XORI_out, SRL_out, SRA_out, ROR_out);

  assign MemToReg = MemRead;
  assign RegDest = R_Type;
endmodule

module Processor (
);

  wire alu_1_jr, alu_1_zero, aluctrl_1_lws, Clock_out, control_unit_1_alusrc, control_unit_1_beq,
       control_unit_1_bneq, control_unit_1_extop, control_unit_1_jal, control_unit_1_jump,
       control_unit_1_lui, control_unit_1_memread, control_unit_1_memtoreg, control_unit_1_memwrite,
       control_unit_1_r_type, control_unit_1_regdest, control_unit_1_regwrite, ex_buffer_1_memread_out,
       ex_buffer_1_memtoreg_out, ex_buffer_1_mw_out, ex_buffer_1_rw_out, id_buffer_1_beq_out,
       id_buffer_1_bneq_out, id_buffer_1_extop_out, id_buffer_1_jal_out, id_buffer_1_jump_out,
       id_buffer_1_memread_out, id_buffer_1_memtoreg_out, id_buffer_1_memwrite_out, id_buffer_1_regdest_out,
       id_buffer_1_regwrite_out, mem_buffer_1_mtr_out, mem_buffer_1_re_out, or_1_out, or_2_out;
  wire [1:0] forward_1_forwarda, forward_1_forwardb;
  wire [2:0] ex_buffer_1_out_9, id_buffer_1_ra_out, id_buffer_1_rb_out, id_buffer_1_rd_out,
       mem_buffer_1_out_7, multiplexer_2_out, multiplexer_3_out, multiplexer_6_out, multiplexer_7_out,
       program_counter_control_1_pc;
  wire [3:0] aluctrl_1_alu_control, control_unit_1_aluop, id_buffer_1_aluop_2;
  wire [4:0] id_buffer_1_imm_out;
  wire [15:0] adder_1_out, adder_2_out, adder_3_out, alu_1_output, bit_extender_1_out, ex_buffer_1_alu_out,
       ex_buffer_1_out_11, extender_1_out, id_buffer_1_bus_a_out, id_buffer_1_bus_b_in_2,
       id_buffer_1_jimm_out, id_buffer_1_pc_out, if_buffer_1_ir_out, if_buffer_1_pc_out,
       mem_buffer_1_alu_out, mem_buffer_1_mem_out, multiplexer_1_out, multiplexer_4_out, multiplexer_5_out,
       multiplexer_8_out, multiplexer_9_out, multiplexer_10_out, multiplexer_11_out, Program_Counter_q,
       ram_1_data, ram_2_data, register_set_1_bus_a, register_set_1_bus_b, shifter_1_out;

  Multiplexer #(.select(3), .width(16), .enable("false")) multiplexer_1 (
    .in0(adder_1_out), .in1(id_buffer_1_jimm_out), .in2(adder_3_out), .in4(adder_3_out),
    .out(multiplexer_1_out), .sel(program_counter_control_1_pc));  // open: in3, in5, in6, in7
  Register #(.width(16)) Program_Counter (
    .D(multiplexer_1_out), .Q(Program_Counter_q), .clk(Clock_out));  // open: en, clr
  Clock Clock (.out(Clock_out));
  Adder #(.width(16)) adder_1 (.a(Program_Counter_q), .b(16'h1), .out(adder_1_out));  // open: cin, cout
  RAM #(.addrWidth(16), .dataWidth(16), .bus("separate")) ram_1 (
    .addr(Program_Counter_q), .data(ram_1_data), .sel(1'b1), .ld(1'b1));  // open: din, str, clk, clr
  IF_Buffer if_buffer_1 (
    .CLK(Clock_out), .PC_in(adder_1_out), .PC_out(if_buffer_1_pc_out), .IR_in(ram_1_data),
    .IR_out(if_buffer_1_ir_out));
  assign bit_extender_1_out = {{5{if_buffer_1_ir_out[10]}}, if_buffer_1_ir_out[10:0]};  // Bit_Extender bit_extender_1
  Shifter #(.width(16)) shifter_1 (.in(bit_extender_1_out), .\dist (4'b0101), .out(shifter_1_out));
  Multiplexer #(.width(3), .enable("false")) multiplexer_2 (
    .in0(if_buffer_1_ir_out[2:0]), .in1(mem_buffer_1_out_7), .out(multiplexer_2_out),
    .sel(control_unit_1_regdest));
  Control_Unit control_unit_1 (
    .JAL(control_unit_1_jal), .Jump(control_unit_1_jump), .RegDest(control_unit_1_regdest),
    .BEQ(control_unit_1_beq), .MemWrite(control_unit_1_memwrite), .MemRead(control_unit_1_memread),
    .MemToReg(control_unit_1_memtoreg), .RegWrite(control_unit_1_regwrite), .BNEQ(control_unit_1_bneq),
    .ALUSrc(control_unit_1_alusrc), .ExtOp(control_unit_1_extop), .ALUOp(control_unit_1_aluop),
    .Opcode(if_buffer_1_ir_out[15:11]), .R_Type(control_unit_1_r_type), .LUI(control_unit_1_lui));
  Adder #(.width(16)) adder_2 (.a(bit_extender_1_out), .b(if_buffer_1_pc_out), .out(adder_2_out));  // open: cin, cout
  Multiplexer #(.width(3), .enable("false")) multiplexer_3 (
    .in0(multiplexer_2_out), .in1(3'b111), .out(multiplexer_3_out), .sel(id_buffer_1_jal_out));
  Multiplexer #(.width(16), .enable("false")) multiplexer_4 (
    .in0(multiplexer_11_out), .in1(id_buffer_1_pc_out), .out(multiplexer_4_out), .sel(id_buffer_1_jal_out));
  Multiplexer #(.width(16), .enable("false")) multiplexer_5 (
    .in0(register_set_1_bus_a), .in1(shifter_1_out), .out(multiplexer_5_out), .sel(control_unit_1_lui));
  Register_Set register_set_1 (
    .Bus_W(multiplexer_4_out), .Bus_A(register_set_1_bus_a), .RA(if_buffer_1_ir_out[5:3]),
    .RB(if_buffer_1_ir_out[2:0]), .Bus_B(register_set_1_bus_b), .RegWrite(mem_buffer_1_re_out),
    .Clock(Clock_out), .RW(multiplexer_3_out));
  ALUCtrl aluctrl_1 (
    .Opcode(if_buffer_1_ir_out[15:11]), .Function(if_buffer_1_ir_out[10:9]),
    .ALU_Control(aluctrl_1_alu_control), .LWS(aluctrl_1_lws), .Main_Control(control_unit_1_aluop),
    .Type(control_unit_1_r_type));
  or or_1 (or_1_out, aluctrl_1_lws, control_unit_1_memtoreg, control_unit_1_memread);
  Multiplexer #(.width(3), .enable("false")) multiplexer_6 (
    .in0(if_buffer_1_ir_out[2:0]), .in1(3'b001), .out(multiplexer_6_out), .sel(control_unit_1_lui));
  Program_Counter_Control program_counter_control_1 (
    .BNE(id_buffer_1_bneq_out), .Zero(alu_1_zero), .BEQ(id_buffer_1_beq_out), .Jump(id_buffer_1_jump_out),
    .Rs(id_buffer_1_ra_out), .JR(alu_1_jr), .PC(program_counter_control_1_pc));
  ID_Buffer id_buffer_1 (
    .JImm_In(adder_2_out), .RA(if_buffer_1_ir_out[5:3]), .RB(multiplexer_6_out),
    .RD(if_buffer_1_ir_out[8:6]), .PC_In(if_buffer_1_pc_out), .Imm_In(if_buffer_1_ir_out[10:6]),
    .Bus_A_In(multiplexer_5_out), .Bus_B_In(register_set_1_bus_b), .ALUOp(aluctrl_1_alu_control),
    .JAL_In(control_unit_1_jal), .Clock(Clock_out), .Jump_In(control_unit_1_jump),
    .RegDest_In(control_unit_1_regdest), .BEQ_In(control_unit_1_beq), .MemWrite_In(control_unit_1_memwrite),
    .MemRead_In(or_1_out), .MemToReg_In(control_unit_1_memtoreg), .RegWrite_In(control_unit_1_regwrite),
    .BNEQ_In(control_unit_1_bneq), .ALUSrc_In(control_unit_1_alusrc), .ExtOp_In(control_unit_1_extop),
    .JImm_Out(id_buffer_1_jimm_out), .RA_Out(id_buffer_1_ra_out), .RB_Out(id_buffer_1_rb_out),
    .RD_Out(id_buffer_1_rd_out), .PC_Out(id_buffer_1_pc_out), .Imm_Out(id_buffer_1_imm_out),
    .Bus_A_Out(id_buffer_1_bus_a_out), .Bus_B_In_2(id_buffer_1_bus_b_in_2), .ALUOp_2(id_buffer_1_aluop_2),
    .JAL_Out(id_buffer_1_jal_out), .Jump_Out(id_buffer_1_jump_out), .RegDest_Out(id_buffer_1_regdest_out),
    .BEQ_Out(id_buffer_1_beq_out), .MemWrite_Out(id_buffer_1_memwrite_out),
    .MemRead_Out(id_buffer_1_memread_out), .MemToReg_Out(id_buffer_1_memtoreg_out),
    .RegWrite_Out(id_buffer_1_regwrite_out), .BNEQ_Out(id_buffer_1_bneq_out),
    .ExtOp_Out(id_buffer_1_extop_out));  // open: ALUSrc_Out
  Adder #(.width(16)) adder_3 (.a(id_buffer_1_pc_out), .b(extender_1_out), .out(adder_3_out));  // open: cin, cout
  Forward forward_1 (
    .ForwardA(forward_1_forwarda), .ForwardB(forward_1_forwardb), .RS(id_buffer_1_ra_out),
    .RD_MEM(ex_buffer_1_out_9), .RD_WB(mem_buffer_1_out_7), .RT(id_buffer_1_rb_out),
    .RegWrite_MEM(ex_buffer_1_rw_out), .RegWrite_WB(mem_buffer_1_re_out));
  Extender extender_1 (.Immediate(id_buffer_1_imm_out), .Out(extender_1_out), .ExtOp(id_buffer_1_extop_out));
  Multiplexer #(.width(3), .enable("false")) multiplexer_7 (
    .in0(id_buffer_1_rb_out), .in1(id_buffer_1_rd_out), .out(multiplexer_7_out), .sel(id_buffer_1_regdest_out));
  Multiplexer #(.select(2), .width(16), .enable("false")) multiplexer_8 (
    .in0(id_buffer_1_bus_a_out), .in1(multiplexer_11_out), .in2(ex_buffer_1_alu_out),
    .out(multiplexer_8_out), .sel(forward_1_forwarda));  // open: in3
  Multiplexer #(.select(2), .width(16), .enable("false")) multiplexer_9 (
    .in0(id_buffer_1_bus_b_in_2), .in1(multiplexer_11_out), .in2(ex_buffer_1_alu_out),
    .out(multiplexer_9_out), .sel(forward_1_forwardb));  // open: in3
  Multiplexer #(.width(16), .enable("false")) multiplexer_10 (
    .in0(multiplexer_9_out), .in1(extender_1_out), .out(multiplexer_10_out), .sel(id_buffer_1_extop_out));
  ALU alu_1 (
    .Output(alu_1_output), .Bus_A(multiplexer_8_out), .Bus_B(multiplexer_10_out),
    .ALUCtrl(id_buffer_1_aluop_2), .JR(alu_1_jr), .Zero(alu_1_zero));
  EX_buffer ex_buffer_1 (
    .in_1(multiplexer_7_out), .ALU_In(alu_1_output), .in_3(multiplexer_9_out), .Clock(Clock_out),
    .MW_In(id_buffer_1_memwrite_out), .MemRead_In(id_buffer_1_memread_out),
    .MemToReg_In(id_buffer_1_memtoreg_out), .RW_In(id_buffer_1_regwrite_out), .out_9(ex_buffer_1_out_9),
    .ALU_Out(ex_buffer_1_alu_out), .out_11(ex_buffer_1_out_11), .MW_Out(ex_buffer_1_mw_out),
    .MemRead_Out(ex_buffer_1_memread_out), .MemToReg_Out(ex_buffer_1_memtoreg_out),
    .RW_Out(ex_buffer_1_rw_out));
  or or_2 (or_2_out, ex_buffer_1_mw_out, ex_buffer_1_memread_out);
  RAM #(.addrWidth(16), .dataWidth(16), .bus("separate")) ram_2 (
    .addr(ex_buffer_1_alu_out), .din(ex_buffer_1_out_11), .data(ram_2_data), .str(ex_buffer_1_mw_out),
    .sel(or_2_out), .clk(Clock_out), .ld(ex_buffer_1_memread_out), .clr(1'b0));
  MEM_Buffer mem_buffer_1 (
    .in_1(ex_buffer_1_out_9), .ALU_In(ex_buffer_1_alu_out), .Mem_In(ram_2_data), .Clock(Clock_out),
    .MTR_In(ex_buffer_1_memtoreg_out), .RW_In(ex_buffer_1_rw_out), .out_7(mem_buffer_1_out_7),
    .ALU_Out(mem_buffer_1_alu_out), .Mem_Out(mem_buffer_1_mem_out), .MTR_Out(mem_buffer_1_mtr_out),
    .RE_Out(mem_buffer_1_re_out));
  Multiplexer #(.width(16), .enable("false")) multiplexer_11 (
    .in0(mem_buffer_1_alu_out), .in1(mem_buffer_1_mem_out), .out(multiplexer_11_out),
    .sel(mem_buffer_1_mtr_out));

  // Notes on the sheet:
  //   Instruction Memory
endmodule
